// Logisim project LAb 4.circ as structural Verilog: 1 circuit, main circuit main
module main (
  input  H,
  input  S,
  input  B,
  input  D,
  input  E,
  output Y
);

  wire and_1_out, and_2_out, and_3_out, and_4_out, and_5_out, not_1_out, not_2_out, not_3_out, not_4_out;

  not not_1 (not_1_out, B);
  not not_2 (not_2_out, D);
  not not_3 (not_3_out, E);
  and and_1 (and_1_out, H, not_3_out);
  and and_2 (and_2_out, S, E, not_1_out);
  not not_4 (not_4_out, S);
  and and_3 (and_3_out, not_2_out, E);
  and and_4 (and_4_out, H, not_3_out);
  and and_5 (and_5_out, not_4_out, B, D);
  or or_1 (Y, and_1_out, and_2_out, and_5_out, and_3_out, and_4_out);
endmodule
