// Logisim project LAb5_item1.circ as structural Verilog: 1 circuit, main circuit main
module main (
  input  s0,
  input  s1,
  input  s2,
  input  s3,
  output a,
  output b,
  output c,
  output d,
  output e,
  output f,
  output g
);

  wire and_1_out, and_2_out, and_3_out, and_4_out, and_5_out, and_6_out, and_7_out, and_8_out, and_9_out,
       and_10_out, and_11_out, and_12_out, and_13_out, and_14_out, not_1_out, not_2_out, not_3_out,
       not_4_out, not_5_out, not_6_out, not_7_out, not_8_out, not_9_out, not_10_out, not_11_out, not_12_out,
       not_13_out, not_14_out, not_15_out, not_16_out, not_17_out, not_18_out, not_19_out;

  not not_1 (not_1_out, s1);
  and and_1 (and_1_out, not_1_out, not_2_out);
  not not_2 (not_2_out, s3);
  and and_2 (and_2_out, s1, s3);
  not not_3 (not_3_out, s1);
  not not_4 (not_4_out, s2);
  and and_3 (and_3_out, not_4_out, not_5_out);
  not not_5 (not_5_out, s3);
  and and_4 (and_4_out, s2, s3);
  not not_6 (not_6_out, s2);
  or or_1 (c, not_6_out, s3, s1);
  not not_7 (not_7_out, s1);
  and and_5 (and_5_out, not_7_out, not_8_out);
  not not_8 (not_8_out, s3);
  not not_9 (not_9_out, s1);
  and and_6 (and_6_out, not_9_out, s2);
  and and_7 (and_7_out, s2, not_10_out);
  not not_10 (not_10_out, s3);
  not not_11 (not_11_out, s2);
  and and_8 (and_8_out, s1, not_11_out, s3);
  not not_12 (not_12_out, s1);
  and and_9 (and_9_out, not_12_out, not_13_out);
  not not_13 (not_13_out, s3);
  and and_10 (and_10_out, s2, not_14_out);
  not not_14 (not_14_out, s3);
  not not_15 (not_15_out, s2);
  and and_11 (and_11_out, not_15_out, not_16_out);
  not not_16 (not_16_out, s3);
  not not_17 (not_17_out, s1);
  and and_12 (and_12_out, not_17_out, s2);
  and and_13 (and_13_out, s1, not_18_out);
  not not_18 (not_18_out, s2);
  and and_14 (and_14_out, s1, not_19_out);
  not not_19 (not_19_out, s3);
  or or_2 (a, and_1_out, s2, and_2_out, s0);
  or or_3 (b, not_3_out, and_3_out, and_4_out);
  or or_4 (d, and_5_out, and_6_out, and_7_out, and_8_out, s0);
  or or_5 (e, and_9_out, and_10_out);
  or or_6 (f, and_11_out, s1, s0);
  or or_7 (g, and_12_out, and_13_out, and_14_out, s0);
endmodule
